// Digital circuit SAPS.dig as structural Verilog
module SAPS (
  input  CLK,
  output [7:0] Data_BUS,
  output [3:0] Address_BUS,
  output C,
  output Z,
  output [3:0] OPCODE,
  output [7:0] A,
  output [7:0] B,
  output [7:0] PC
);

  wire alu_1_c, alu_1_n, alu_1_z, and_2_out, and_3_out, cc_1_p2, control_1_ai, control_1_ao, control_1_b0,
       control_1_b1, control_1_bi, control_1_ce, control_1_co, control_1_fi, control_1_hlt, control_1_ii,
       control_1_io, control_1_j, control_1_mi, control_1_ro, control_1_sh, control_1_su, multiplexer_2_out,
       multiplexer_3_out, not_1_out, not_2_out;
  wire [1:0] control_1_m;
  wire [3:0] ir_1_i_2, multiplexer_4_out;
  wire [7:0] alu_1_out, multiplexer_1_out, rom_1_d;
  wire [9:0] flag_1_n;

  // CC cc_1: pin names not known; wires that end beside it: 1'b1, cc_1_p2, flag_1_n[0], flag_1_n[1], flag_1_n[2]
  not not_1 (not_1_out, control_1_hlt);
  and and_1 (cc_1_p2, CLK, not_1_out);
  Control control_1 (
    .IN({flag_1_n[9], Z, C, OPCODE, flag_1_n[2:0]}), .HLT(control_1_hlt), .MI(control_1_mi),
    .RO(control_1_ro), .IO(control_1_io), .II(control_1_ii), .AI(control_1_ai), .EO(control_1_m[1]),
    .SU(control_1_su), .BI(control_1_bi), .CE(control_1_ce), .CO(control_1_co), .J(control_1_j),
    .FI(control_1_fi), .AO(control_1_ao), .SH(control_1_sh), .M(control_1_m[0]), .B1(control_1_b1),
    .B0(control_1_b0));  // open: RI, OI
  Multiplexer #(.Selector_Bits(2), .Bits(8)) multiplexer_1 (
    .sel(control_1_m), .in_0(B), .in_1(B), .in_2({8{1'b1}}), .in_3({8{1'b0}}), .out(multiplexer_1_out));
  not not_2 (not_2_out, control_1_m[0]);
  Multiplexer multiplexer_2 (.sel(and_2_out), .in_0(control_1_b1), .in_1(1'b0), .out(multiplexer_2_out));
  Multiplexer multiplexer_3 (.sel(and_2_out), .in_0(control_1_b0), .in_1(1'b0), .out(multiplexer_3_out));
  and and_2 (and_2_out, control_1_m[1], not_2_out);
  ALU alu_1 (
    .SH(control_1_sh), .M(control_1_m[0]), .B1(multiplexer_2_out), .B0(multiplexer_3_out),
    .Sub(control_1_su), .A(A), .B(multiplexer_1_out), .Z(alu_1_z), .C(alu_1_c), .N(alu_1_n), .Out(alu_1_out));
  RegisterA registera_1 (.A(Data_BUS), .CLK(cc_1_p2), .A_in(control_1_ai), .A_2(A));
  FLAG flag_1 (
    .CLK(cc_1_p2), .en(control_1_fi), .Z_2(alu_1_z), .C_2(alu_1_c), .N_2(alu_1_n), .Z(Z), .C(C),
    .N(flag_1_n[9]));
  assign Data_BUS = control_1_m[1] ? alu_1_out : 8'bz;  // Driver driver_1
  assign Data_BUS = control_1_ao ? A : 8'bz;  // Driver driver_2
  and and_3 (and_3_out, control_1_io, control_1_ai);
  IR ir_1 (.I(Data_BUS), .CLK(cc_1_p2), .I_in(control_1_ii), .I_2({OPCODE, ir_1_i_2}));
  // RegisterB registerb_1: pin names not known; wires that end beside it: Data_BUS, cc_1_p2, control_1_bi, B
  // MAR mar_1: pin names not known; wires that end beside it: Data_BUS, cc_1_p2, control_1_mi, Address_BUS, flag_1_n[9]
  PC pc_1 (.en(control_1_ce), .CLK(cc_1_p2), .J(control_1_j), .I(Data_BUS), .P(PC));
  ROM #(.AddrBits(4), .Bits(8)) rom_1 (.A(Address_BUS), .sel(1'b1), .D(rom_1_d));
  assign Data_BUS = control_1_ro ? rom_1_d : 8'bz;  // Driver driver_3
  Multiplexer #(.Bits(4)) multiplexer_4 (.sel(and_3_out), .in_0(OPCODE), .in_1(4'b0000), .out(multiplexer_4_out));
  assign Data_BUS = control_1_co ? PC : 8'bz;  // Driver driver_4
  assign Data_BUS = control_1_io ? {multiplexer_4_out, ir_1_i_2} : 8'bz;  // Driver driver_5

  // Notes on the sheet:
  //   CLK: Hz: 100
  //   contents of rom_1 (hex, n*v repeats v):
  //   1d,2c,87,7a,ee,be,0,ef,2e,9e,0,0,0,55,1,ff
endmodule
